# Fritzing sketch esp8266温湿度+显示器+按钮 (saved by Fritzing 1.0.5)
breadboards: 1

parts:
  DHT1 = Humidity and Temperature Sensor DHT11
  OLED_I2C1 = OLED 128x64 I2C Monochrome Display
  R1 = Resistor [tolerance=±5% power=0.25W resistance=4.7k package=THT]
  Mod1 = Amica NodeMCU DEVKIT 1.0
  S1 = Pushbutton [package="[THT]"]
  S2 = Pushbutton [package="[THT]"]
  R2 = Resistor [tolerance=±5% power=0.25W resistance=220 package=THT]
  R3 = Resistor [tolerance=±5% power=0.25W resistance=220 package=THT]

nets:
  VCC: DHT1.Vcc, OLED_I2C1.VDD, R1.Pin_0, Mod1.pin1, Mod1.pin_10, Mod1.pin_26, S1.Pin_3, S1.Pin_4, S2.Pin_3, S2.Pin_4
  N1: DHT1.Data-signal, R1.Pin_1, Mod1.pin_13
  N2: DHT1.GND_2, OLED_I2C1.GND, Mod1.pin2, Mod1.pin_9, Mod1.pin_25, Mod1.pin_29, R2.Pin_1, R3.Pin_1
  N3: OLED_I2C1.SDA, Mod1.pin_11
  N4: OLED_I2C1.SCK, Mod1.pin_12
  N5: Mod1.pin7, S2.Pin_1, S2.Pin_2, R3.Pin_0
  N6: Mod1.pin8, S1.Pin_1, S1.Pin_2, R2.Pin_0

custom parts:
  Humidity and Temperature Sensor DHT11: Digital relative humidity & temperature sensor DHT11
