# Fritzing sketch esp8266温湿度+显示器 (saved by Fritzing 1.0.5)
breadboards: 1

parts:
  DHT1 = Humidity and Temperature Sensor DHT11
  OLED_I2C1 = OLED 128x64 I2C Monochrome Display
  R1 = Resistor [tolerance=±5% power=0.25W resistance=4.7k package=THT]
  Mod1 = Amica NodeMCU DEVKIT 1.0

nets:
  VCC: DHT1.Vcc, OLED_I2C1.VDD, R1.Pin_0, Mod1.pin1, Mod1.pin_10, Mod1.pin_26
  N1: DHT1.Data-signal, R1.Pin_1, Mod1.pin_13
  N2: DHT1.GND_2, OLED_I2C1.GND, Mod1.pin2, Mod1.pin_9, Mod1.pin_25, Mod1.pin_29
  N3: OLED_I2C1.SDA, Mod1.pin_11
  N4: OLED_I2C1.SCK, Mod1.pin_12

custom parts:
  Humidity and Temperature Sensor DHT11: Digital relative humidity & temperature sensor DHT11
