# Fritzing sketch esp8266温湿度 (saved by Fritzing 1.0.5)
breadboards: 1

parts:
  DHT1 = Humidity and Temperature Sensor DHT11
  R1 = Resistor [tolerance=±5% power=0.25W resistance=4.7k package=THT]
  Mod1 = Amica NodeMCU DEVKIT 1.0

nets:
  N1: DHT1.Vcc, R1.Pin_0, Mod1.pin1, Mod1.pin_10, Mod1.pin_26
  N2: DHT1.Data-signal, R1.Pin_1, Mod1.pin_13
  N3: DHT1.GND_2, Mod1.pin2, Mod1.pin_9, Mod1.pin_25, Mod1.pin_29

custom parts:
  Humidity and Temperature Sensor DHT11: Digital relative humidity & temperature sensor DHT11
