# Fritzing sketch uno温湿度+显示器 (saved by Fritzing 1.0.5)
breadboards: 1

parts:
  DHT1 = Humidity and Temperature Sensor DHT11
  OLED_I2C1 = OLED 128x64 I2C Monochrome Display
  元件1 = Arduino Uno (Rev3)
  R1 = Resistor [tolerance=±5% power=0.25W resistance=4.7k package=THT]

nets:
  VCC: DHT1.Vcc, OLED_I2C1.VDD, 元件1.5V, R1.Pin_0
  N1: DHT1.Data-signal, 元件1.D2, R1.Pin_1
  GND: DHT1.GND_2, OLED_I2C1.GND, 元件1.GND
  N2: OLED_I2C1.SCK, 元件1.D3_PWM

custom parts:
  Humidity and Temperature Sensor DHT11: Digital relative humidity & temperature sensor DHT11
