# Fritzing sketch uno温湿度 (saved by Fritzing 1.0.5)
breadboards: 1

parts:
  DHT1 = Humidity and Temperature Sensor DHT11
  元件1 = Arduino Uno (Rev3)
  R1 = Resistor [tolerance=±5% power=0.25W resistance=4.7k package=THT]

nets:
  VCC: DHT1.Vcc, 元件1.5V, R1.Pin_0
  N1: DHT1.Data-signal, 元件1.D2, R1.Pin_1
  N2: DHT1.GND_2, 元件1.GND

custom parts:
  Humidity and Temperature Sensor DHT11: Digital relative humidity & temperature sensor DHT11
