# Fritzing sketch main (saved by Fritzing 1.0.5)
breadboards: 1

parts:
  元件1 = Arduino Uno (Rev3)
  J1 = Basic Servo
  J2 = Piezo Speaker
  hc-sr2 = hc-sr04

nets:
  GND: 元件1.GND, J1.gnd, hc-sr2.GND
  N1: 元件1.D2, J1.pulse
  N2: 元件1.D3_PWM, J2.pin2
  N3: 元件1.D4, hc-sr2.Trig
  N4: 元件1.D5_PWM, hc-sr2.Echo
  VCC: 元件1.5V, J1.vcc, hc-sr2.VCC
